// Logisim project DDCA PROJECT.circ as structural Verilog: 1 circuit, main circuit main
module main (
  input  [3:0] LIGHT_PIN
);

  wire comparator_1_lt;

  Hex_Digit_Display hex_digit_display_1 (.value(LIGHT_PIN));  // open: dp
  Comparator #(.width(4), .mode("unsigned")) comparator_1 (
    .a(LIGHT_PIN), .b(4'b0110), .lt(comparator_1_lt));  // open: gt, eq
  LED LAMP (.in(comparator_1_lt));

  // Notes on the sheet:
  //   SENSOR
  //   THRESHOLD
endmodule
