// Logisim project FULLadder.circ as structural Verilog: 1 circuit, main circuit main
module main (
  input  A,
  input  B,
  input  Cin,
  output SUM,
  output out_5
);

  wire AND_2_out, AND_out, XOR_out;

  xor XOR (XOR_out, A, B);
  xor XOR_2 (SUM, XOR_out, Cin);
  and AND (AND_out, Cin, XOR_out);
  and AND_2 (AND_2_out, A, B);
  or OR (out_5, AND_out, AND_2_out);

  // Notes on the sheet:
  //   CARRY-OUT (Cout)
endmodule
